// Logisim project Binary-To-Gray.circ as structural Verilog: 1 circuit, main circuit main
module main (
  input  D,
  input  C,
  input  B,
  input  A,
  output G3,
  output G2,
  output G1,
  output G0
);

  xor xor_1 (G2, D, C);
  xor xor_2 (G1, C, B);
  xor xor_3 (G0, B, A);

  assign G3 = D;
endmodule
