// Logisim project Counters.circ as structural Verilog: 1 circuit, main circuit main
module main (
  input  Enable,
  input  Preset
);

  wire button_1_out, j_k_ff_1_q, j_k_ff_2_q, j_k_ff_3_q, j_k_ff_4_q, nand_1_out;

  Button button_1 (.out(button_1_out));
  LED led_1 (.in(j_k_ff_1_q));
  J_K_Flip_Flop j_k_ff_1 (
    .J(1'b1), .clk(button_1_out), .K(1'b1), .Q(j_k_ff_1_q), .preset(Preset), .en(Enable), .reset(nand_1_out));  // open: Qn
  LED led_2 (.in(j_k_ff_2_q));
  J_K_Flip_Flop j_k_ff_2 (
    .J(1'b1), .clk(j_k_ff_1_q), .K(1'b1), .Q(j_k_ff_2_q), .preset(Preset), .en(Enable), .reset(nand_1_out));  // open: Qn
  nand nand_1 (nand_1_out, j_k_ff_2_q, j_k_ff_4_q);
  J_K_Flip_Flop j_k_ff_3 (
    .J(1'b1), .clk(j_k_ff_2_q), .K(1'b1), .Q(j_k_ff_3_q), .preset(Preset), .en(Enable), .reset(nand_1_out));  // open: Qn
  LED led_3 (.in(j_k_ff_3_q));
  LED led_4 (.in(j_k_ff_4_q));
  J_K_Flip_Flop j_k_ff_4 (
    .J(1'b1), .clk(j_k_ff_3_q), .K(1'b1), .Q(j_k_ff_4_q), .preset(Preset), .en(Enable), .reset(nand_1_out));  // open: Qn

  // Notes on the sheet:
  //   MOD - 10 Asynchronous Counter
endmodule
