// Logisim project D Flip Flop.circ as structural Verilog: 1 circuit, main circuit main
module main (
  input  D,
  input  Preset,
  input  Clear
);

  wire Clock_out, d_ff_1_q, d_ff_1_qn;

  Button Clock (.out(Clock_out));
  LED Q (.in(d_ff_1_q));
  D_Flip_Flop d_ff_1 (.clk(Clock_out), .D(D), .Q(d_ff_1_q), .Qn(d_ff_1_qn), .preset(Preset), .en(1'b1), .reset(Clear));
  LED Q_prime (.in(d_ff_1_qn));

  // Notes on the sheet:
  //   IC7474 D - Flip-Flop
endmodule
