// Logisim project DeMUX.circ as structural Verilog: 1 circuit, main circuit main
module main (
);

  wire _7411_2_out, _7411_3_out, _7411_4_out, _7411_out, button_1_out, button_2_out, not_1_out, not_2_out;

  Button button_1 (.out(button_1_out));
  not not_1 (not_1_out, button_1_out);
  Button button_2 (.out(button_2_out));
  not not_2 (not_2_out, button_2_out);
  and _7411 (_7411_out, 1'b1, not_1_out, not_2_out);
  LED led_1 (.in(_7411_out));
  LED led_2 (.in(_7411_2_out));
  and _7411_2 (_7411_2_out, 1'b1, not_1_out, button_2_out);
  LED led_3 (.in(_7411_3_out));
  and _7411_3 (_7411_3_out, 1'b1, button_1_out, not_2_out);
  LED led_4 (.in(_7411_4_out));
  and _7411_4 (_7411_4_out, 1'b1, button_1_out, button_2_out);

  // Notes on the sheet:
  //   Din
  //   s1
  //   7404
  //   s0
  //   7404
  //   Y0
  //   Y1
  //   Y2
  //   Y3
endmodule
