// Logisim project Decoder SOP.circ as structural Verilog: 1 circuit, main circuit main
module main (
  input  in_1,
  input  [2:0] in_2
);

  wire CARRY_out, decoder_1_out1, decoder_1_out2, decoder_1_out3, decoder_1_out4, decoder_1_out5,
       decoder_1_out6, decoder_1_out7, SUM_out;

  Decoder #(.select(3)) decoder_1 (
    .out1(decoder_1_out1), .out2(decoder_1_out2), .out3(decoder_1_out3), .out4(decoder_1_out4),
    .out5(decoder_1_out5), .out6(decoder_1_out6), .out7(decoder_1_out7), .sel(in_2), .en(in_1));  // open: out0
  or SUM (SUM_out, decoder_1_out1, decoder_1_out2, decoder_1_out4, decoder_1_out7);
  or CARRY (CARRY_out, decoder_1_out3, decoder_1_out5, decoder_1_out6, decoder_1_out7);
  LED led_1 (.in(SUM_out));
  LED led_2 (.in(CARRY_out));

  // Notes on the sheet:
  //   SUM = m(1, 2, 4, 7)
  //   CARRY = m(3, 5, 6, 7)
endmodule
