// Logisim project Gray to Binary.circ as structural Verilog: 1 circuit, main circuit main
module main (
  input  G3,
  input  G2,
  input  G1,
  input  G0,
  output D,
  output C,
  output B,
  output A
);

  wire xor_2_out, xor_3_out, xor_4_out;

  xor xor_1 (C, G3, G2);
  xor xor_2 (xor_2_out, G3, G2);
  xor xor_3 (xor_3_out, G3, G2);
  xor xor_4 (xor_4_out, G1, G0);
  xor xor_5 (B, xor_2_out, G1);
  xor xor_6 (A, xor_3_out, xor_4_out);

  assign D = G3;
endmodule
