// Logisim project JK Flip Flop.circ as structural Verilog: 1 circuit, main circuit main
module main (
  input  J,
  input  K,
  input  En,
  input  Preset,
  input  Clear
);

  wire Clock_out, j_k_ff_1_q, j_k_ff_1_qn;

  Button Clock (.out(Clock_out));
  J_K_Flip_Flop j_k_ff_1 (
    .J(J), .clk(Clock_out), .K(K), .Q(j_k_ff_1_q), .Qn(j_k_ff_1_qn), .preset(Preset), .en(En), .reset(Clear));
  LED Q (.in(j_k_ff_1_q));
  LED Q_prime (.in(j_k_ff_1_qn));

  // Notes on the sheet:
  //   IC 7473 JK Flip Flopp
endmodule
