// Logisim project MUX SOP.circ as structural Verilog: 1 circuit, main circuit main
module main (
  input  A,
  input  [1:0] B_C
);

  wire multiplexer_1_out, not_1_out;

  not not_1 (not_1_out, A);
  Multiplexer #(.select(2)) multiplexer_1 (
    .in0(1'b1), .in1(not_1_out), .in2(A), .in3(A), .out(multiplexer_1_out), .sel(B_C), .en(1'b1));
  LED led_1 (.in(multiplexer_1_out));

  // Notes on the sheet:
  //   F(A, B, C) =  m(0, 1, 4, 6, 7)
endmodule
