// Logisim project PIPO Shift Registe.circ as structural Verilog: 1 circuit, main circuit main
module main (
  input  A,
  input  B,
  input  C,
  input  Clear,
  input  Preset,
  input  Enable
);

  wire Clock_out, d_ff_1_q, d_ff_2_q, d_ff_3_q;

  Button Clock (.out(Clock_out));
  D_Flip_Flop d_ff_1 (.clk(Clock_out), .D(A), .Q(d_ff_1_q), .preset(Preset), .en(Enable), .reset(Clear));  // open: Qn
  LED Qa (.in(d_ff_1_q));
  D_Flip_Flop d_ff_2 (.clk(Clock_out), .D(B), .Q(d_ff_2_q), .preset(Preset), .reset(Enable));  // open: Qn, en
  LED Qb (.in(d_ff_2_q));
  LED Qc (.in(d_ff_3_q));
  D_Flip_Flop d_ff_3 (.clk(Clock_out), .D(C), .Q(d_ff_3_q), .preset(Preset), .en(Enable), .reset(Clear));  // open: Qn

  // Notes on the sheet:
  //   Parallel In Parallel Out Shift Register
endmodule
