// Logisim project SISO Shift Register.circ as structural Verilog: 1 circuit, main circuit main
module main (
  input  Din,
  input  Clear,
  input  Preset,
  input  Enable
);

  wire Clock_out, d_ff_1_q, d_ff_2_q, d_ff_3_q;

  Button Clock (.out(Clock_out));
  D_Flip_Flop d_ff_1 (.clk(Clock_out), .D(Din), .Q(d_ff_1_q), .preset(Preset), .en(Enable), .reset(Clear));  // open: Qn
  LED Qa (.in(d_ff_1_q));
  D_Flip_Flop d_ff_2 (
    .clk(Clock_out), .D(d_ff_1_q), .Q(d_ff_2_q), .preset(Preset), .en(Enable), .reset(Clear));  // open: Qn
  LED Qc (.in(d_ff_3_q));
  LED Qb (.in(d_ff_2_q));
  D_Flip_Flop d_ff_3 (
    .clk(Clock_out), .D(d_ff_2_q), .Q(d_ff_3_q), .preset(Preset), .en(Enable), .reset(Clear));  // open: Qn

  // Notes on the sheet:
  //   Serial In Serial Out Shift Register
endmodule
