// Logisim project Synchronous Counter.circ as structural Verilog: 1 circuit, main circuit main
module main (
  input  Preset,
  input  Enable
);

  wire and_1_out, Clear_out, Clock_out, j_k_ff_1_q, j_k_ff_2_q, j_k_ff_3_q;

  Button Clock (.out(Clock_out));
  J_K_Flip_Flop j_k_ff_1 (
    .J(1'b1), .clk(Clock_out), .K(1'b1), .Q(j_k_ff_1_q), .preset(Preset), .en(Enable), .reset(Clear_out));  // open: Qn
  Button Clear (.out(Clear_out));
  LED led_1 (.in(j_k_ff_1_q));
  J_K_Flip_Flop j_k_ff_2 (
    .J(j_k_ff_1_q), .clk(Clock_out), .K(j_k_ff_1_q), .Q(j_k_ff_2_q), .preset(Preset), .en(Enable),
    .reset(Clear_out));  // open: Qn
  LED led_2 (.in(j_k_ff_2_q));
  and and_1 (and_1_out, j_k_ff_1_q, j_k_ff_2_q);
  J_K_Flip_Flop j_k_ff_3 (
    .J(and_1_out), .clk(Clock_out), .K(and_1_out), .Q(j_k_ff_3_q), .preset(Preset), .en(Enable),
    .reset(Clear_out));  // open: Qn
  LED led_3 (.in(j_k_ff_3_q));

  // Notes on the sheet:
  //   3 Bit Synchronous Counter
endmodule
