// Logisim project test.circ as structural Verilog: 1 circuit, main circuit main
module main (
);

  wire and_1_out, button_1_out, button_2_out;

  Button button_1 (.out(button_1_out));
  Button button_2 (.out(button_2_out));
  and and_1 (and_1_out, button_1_out, button_2_out);
  LED led_1 (.in(and_1_out));
endmodule
